# Fritzing sketch Sensor-Wiring (saved by Fritzing 0.9.3b)

parts:
  J1 = Infrared Proximity Sensor
  Raspberry_Pi_1 = Raspberry Pi 3 [part_number=RPI-3-V1.2]

nets:
  N1: J1.Vout, Raspberry_Pi_1.GPIO17
  GND: J1.GND, Raspberry_Pi_1.GND
  VCC: J1.Vcc, Raspberry_Pi_1.5V
